// Logisim project CPUComponents.circ as structural Verilog: 8 circuits, main circuit ALU
module InstructionDecode (
  input  [31:0] Instruction,
  output [10:0] opcode,
  output [4:0] rn,
  output [4:0] rm,
  output [4:0] rd_rt,
  output [5:0] shamt,
  output [31:0] Sign_Ext_0_31,
  output [10:0] opcodeALU
);


  assign opcode = Instruction[31:21];
  assign opcodeALU = Instruction[31:21];
  assign rd_rt = Instruction[4:0];
  assign rm = Instruction[20:16];
  assign rn = Instruction[9:5];
  assign shamt = Instruction[15:10];
  assign Sign_Ext_0_31 = Instruction;

  // Notes on the sheet:
  //   F19
  //   R-type
endmodule

module Registers (
  input  Write,
  input  [4:0] ReadRegister1,
  input  [4:0] ReadRegister2,
  input  [4:0] WriteRegister,
  input  [31:0] WriteData,
  input  Clear,
  input  Clock,
  output [31:0] ReadData1,
  output [31:0] ReadData2
);

  wire and_1_out, demultiplexer_1_out0, demultiplexer_1_out1, demultiplexer_1_out2, demultiplexer_1_out3,
       demultiplexer_1_out4, demultiplexer_1_out5, demultiplexer_1_out6, demultiplexer_1_out7, not_1_out;
  wire [31:0] _0_3_p7, _0_3_p8, _4_7_p7, _4_7_p8, _8_11_p7, _8_11_p8, _12_15_p7, _12_15_p8, _16_19_p7,
       _16_19_p8, _20_23_p7, _20_23_p8, _24_27_p7, _24_27_p8, _28_31_p7, _28_31_p8;

  Demultiplexer #(.select(3), .enable("false")) demultiplexer_1 (
    .out0(demultiplexer_1_out0), .out1(demultiplexer_1_out1), .out2(demultiplexer_1_out2),
    .out3(demultiplexer_1_out3), .out4(demultiplexer_1_out4), .out5(demultiplexer_1_out5),
    .out6(demultiplexer_1_out6), .out7(demultiplexer_1_out7), .in(and_1_out), .sel(WriteRegister[4:2]));
  and and_1 (and_1_out, Write, not_1_out);
  not not_1 (not_1_out, Clock);
  // Registers4 _0_3: pin names not known; wires that end beside it: ReadRegister1[1:0], ReadRegister2[1:0], WriteRegister[1:0], WriteData, demultiplexer_1_out0, Clear, _0_3_p7, _0_3_p8
  // Registers4 _4_7: pin names not known; wires that end beside it: ReadRegister1[1:0], ReadRegister2[1:0], WriteRegister[1:0], WriteData, demultiplexer_1_out1, Clear, _4_7_p7, _4_7_p8
  // Registers4 _8_11: pin names not known; wires that end beside it: ReadRegister1[1:0], ReadRegister2[1:0], WriteRegister[1:0], WriteData, demultiplexer_1_out2, Clear, _8_11_p7, _8_11_p8
  // Registers4 _12_15: pin names not known; wires that end beside it: ReadRegister1[1:0], ReadRegister2[1:0], WriteRegister[1:0], WriteData, demultiplexer_1_out3, Clear, _12_15_p7, _12_15_p8
  // Registers4 _16_19: pin names not known; wires that end beside it: ReadRegister1[1:0], ReadRegister2[1:0], WriteRegister[1:0], WriteData, demultiplexer_1_out4, Clear, _16_19_p7, _16_19_p8
  // Registers4 _20_23: pin names not known; wires that end beside it: ReadRegister1[1:0], ReadRegister2[1:0], WriteRegister[1:0], WriteData, demultiplexer_1_out5, Clear, _20_23_p7, _20_23_p8
  // Registers4 _24_27: pin names not known; wires that end beside it: ReadRegister1[1:0], ReadRegister2[1:0], WriteRegister[1:0], WriteData, demultiplexer_1_out6, Clear, _24_27_p7, _24_27_p8
  // Registers4Z _28_31: pin names not known; wires that end beside it: ReadRegister1[1:0], ReadRegister2[1:0], WriteRegister[1:0], WriteData, demultiplexer_1_out7, Clear, _28_31_p7, _28_31_p8
  Multiplexer #(.select(3), .width(32), .enable("false")) multiplexer_1 (
    .in0(_0_3_p7), .in1(_4_7_p7), .in2(_8_11_p7), .in3(_12_15_p7), .in4(_16_19_p7), .in5(_20_23_p7),
    .in6(_24_27_p7), .in7(_28_31_p7), .out(ReadData1), .sel(ReadRegister1[4:2]));
  Multiplexer #(.select(3), .width(32), .enable("false")) multiplexer_2 (
    .in0(_0_3_p8), .in1(_4_7_p8), .in2(_8_11_p8), .in3(_12_15_p8), .in4(_16_19_p8), .in5(_20_23_p8),
    .in6(_24_27_p8), .in7(_28_31_p8), .out(ReadData2), .sel(ReadRegister2[4:2]));
endmodule

module SignExtend (
  input  [31:0] _0_31,
  output [31:0] out_2
);

  Multiplexer #(.select(2), .width(32), .enable("false")) multiplexer_1 (
    .in0({32{1'b0}}), .in1({{7{_0_31[25]}}, _0_31[24:0]}), .in2({{24{_0_31[20]}}, _0_31[19:12]}),
    .in3({{14{_0_31[23]}}, _0_31[22:5]}), .out(out_2), .sel({_0_31[31], _0_31[26]}));
endmodule

module ALU (
  input  [31:0] A,
  input  [31:0] B,
  input  [3:0] Operation,
  output Zero,
  output [31:0] Result,
  output Sign,
  output Overflow,
  output Carry_Out
);

  wire getsign_1_p2, getsign_2_p2;
  wire [31:0] adder_1_out, and_1_out, getsign_1_p3, getsign_2_p3, getsign_3_p3, multiplexer_1_out,
       multiplexer_2_out, not_1_out, not_2_out, or_1_out;

  assign not_1_out = ~A;  // NOT_Gate not_1, 32 bits wide
  assign not_2_out = ~B;  // NOT_Gate not_2, 32 bits wide
  Multiplexer #(.width(32), .enable("false")) multiplexer_1 (
    .in0(A), .in1(not_1_out), .out(multiplexer_1_out), .sel(Operation[3]));
  Multiplexer #(.width(32), .enable("false")) multiplexer_2 (
    .in0(B), .in1(not_2_out), .out(multiplexer_2_out), .sel(Operation[2]));
  // GetSign getsign_1: pin names not known; wires that end beside it: multiplexer_1_out, getsign_1_p2, getsign_1_p3
  // GetSign getsign_2: pin names not known; wires that end beside it: multiplexer_2_out, getsign_2_p2, getsign_2_p3
  // Overflow overflow_1: pin names not known; wires that end beside it: getsign_1_p2, getsign_2_p2, Sign, Operation[1:0], Overflow
  assign and_1_out = getsign_1_p3 & getsign_2_p3;  // AND_Gate and_1, 32 bits wide
  assign or_1_out = getsign_1_p3 | getsign_2_p3;  // OR_Gate or_1, 32 bits wide
  Adder #(.width(32)) adder_1 (
    .a(getsign_1_p3), .b(getsign_2_p3), .out(adder_1_out), .cin(Operation[2]), .cout(Carry_Out));
  // GetSign getsign_3: pin names not known; wires that end beside it: adder_1_out, Sign, getsign_3_p3
  Multiplexer #(.select(2), .width(32), .enable("false")) multiplexer_3 (
    .in0(and_1_out), .in1(or_1_out), .in2(getsign_3_p3), .in3(B), .out(Result), .sel(Operation[1:0]));
  // Zero zero_1: pin names not known; wires that end beside it: Result, Zero

  // Notes on the sheet:
  //   +/-
  //   +/-
  //   +/-
  //   0?
endmodule

module BranchAddress (
  input  [31:0] PC,
  input  [31:0] Address,
  output [31:0] BranchAddress
);

  Adder #(.width(32)) adder_1 (.a(PC), .b({Address[29:0], 2'b00}), .out(BranchAddress));  // open: cin, cout

  // Notes on the sheet:
  //   Mia McDuffie
  //   10/27/2019
  //   offset
endmodule

// I-Mem
module Inst_Mem_Interface (
  input  [31:0] Instruction_Address,
  input  [31:0] Mem_To_Interface,
  output [31:0] Instruction,
  output [7:0] To_Inst_Mem
);

  // WordAddress wordaddress_1: pin names not known; wires that end beside it: Instruction_Address, To_Inst_Mem

  assign Instruction = Mem_To_Interface;
endmodule

// D Mem
module Data_Mem_Interface (
  input  MemWrite,
  input  MemRead,
  input  [31:0] Data_Address,
  input  [31:0] Data_to_Memory,
  input  [31:0] Data_To_Mem,
  input  Clock___Rising_Edge,
  output [31:0] Data_from_Memory,
  output [7:0] Address_To_Mem,
  output [31:0] Data_From_Mem,
  output [1:0] Mem_Control
);

  wire not_1_out;

  not not_1 (not_1_out, Clock___Rising_Edge);
  // WordAddress wordaddress_1: pin names not known; wires that end beside it: Data_Address, Address_To_Mem
  and and_1 (Mem_Control[0], not_1_out, MemWrite);
  // MemoryData memorydata_1: pin names not known; wires that end beside it: Data_to_Memory, Data_To_Mem, MemWrite, MemRead, Data_from_Memory, Data_From_Mem

  assign Mem_Control[1] = MemRead;
endmodule

module BranchControl (
  input  UnconditionalBranch,
  input  ConditionalBranch__CBZ,
  input  Zero,
  output control
);

  wire and_1_out;

  and and_1 (and_1_out, ConditionalBranch__CBZ, Zero);
  or or_1 (control, UnconditionalBranch, and_1_out);
endmodule
